// Digital circuit ex3_c.dig as structural Verilog
module ex3_c (
  input  clk
);

  wire and_1_out, and_2_out, and_3_out, and_4_out, and_5_out, not_1_out, not_2_out, not_3_out, not_4_out,
       not_5_out, not_6_out;
  wire [3:0] d_ff_1_q, or_3_out;

  D_FF #(.Bits(4), .Default(13)) d_ff_1 (.D(or_3_out), .C(clk), .Q(d_ff_1_q));  // open: nQ
  not not_1 (not_1_out, d_ff_1_q[0]);
  not not_2 (not_2_out, d_ff_1_q[2]);
  not not_3 (not_3_out, d_ff_1_q[3]);
  not not_4 (not_4_out, d_ff_1_q[1]);
  not not_5 (not_5_out, d_ff_1_q[2]);
  not not_6 (not_6_out, d_ff_1_q[3]);
  and and_1 (and_1_out, not_1_out, d_ff_1_q[1]);
  and and_2 (and_2_out, not_2_out, d_ff_1_q[0]);
  and and_3 (and_3_out, not_3_out, not_4_out);
  and and_4 (and_4_out, d_ff_1_q[2], d_ff_1_q[1]);
  and and_5 (and_5_out, d_ff_1_q[3], not_5_out);
  or or_1 (or_3_out[2], and_2_out, and_3_out);
  or or_2 (or_3_out[3], and_4_out, and_5_out);
  or or_3 (or_3_out[0], d_ff_1_q[1], not_6_out);
  or or_4 (or_3_out[1], d_ff_1_q[2], and_1_out);
  LED Q_3 (.in(or_3_out[3]));
  LED Q_1 (.in(or_3_out[1]));
  LED Q_2 (.in(or_3_out[2]));
  LED Q_0 (.in(or_3_out[0]));
endmodule
