// Digital circuit ex3_d.dig as structural Verilog
module ex3_d (
  input  clk
);

  wire [3:0] d_ff_1_q, rom_1_d;

  ROM #(.AddrBits(4), .Bits(4)) rom_1 (.A(d_ff_1_q), .sel(1'b1), .D(rom_1_d));
  D_FF #(.Bits(4)) d_ff_1 (.D(rom_1_d), .C(clk), .Q(d_ff_1_q));  // open: nQ
  LED led_1 (.in(d_ff_1_q[2]));
  LED led_2 (.in(d_ff_1_q[3]));
  LED led_3 (.in(d_ff_1_q[0]));
  LED led_4 (.in(d_ff_1_q[1]));

  // Notes on the sheet:
  //   contents of rom_1 (hex, n*v repeats v):
  //   2,2,3,5,2,7,2,b,2,2,2,d,4*2
endmodule
