// Digital circuit ex4_b.dig as structural Verilog
module ex4_b (
  input  clk
);

  wire [2:0] xor_1_out;
  wire [2:1] d_ff_1_q;

  D_FF #(.Bits(3)) d_ff_1 (.D(xor_1_out), .C(clk), .Q({d_ff_1_q, xor_1_out[2]}));  // open: nQ
  nor nor_1 (xor_1_out[0], d_ff_1_q[1], xor_1_out[2]);
  xor xor_1 (xor_1_out[1], d_ff_1_q[2], d_ff_1_q[1]);
  LED Q_1 (.in(xor_1_out[1]));
  LED Q_2 (.in(xor_1_out[2]));
  LED Q_0 (.in(xor_1_out[0]));

  // Notes on the sheet:
  //   Q2    Q1    Q0
endmodule
