// Digital circuit ex4_c.dig as structural Verilog
module ex4_c (
  input  clk
);

  wire [2:0] d_ff_1_q, rom_1_d;

  ROM #(.AddrBits(3), .Bits(3)) rom_1 (.A(d_ff_1_q), .sel(1'b1), .D(rom_1_d));
  D_FF #(.Bits(3)) d_ff_1 (.D(rom_1_d), .C(clk), .Q(d_ff_1_q));  // open: nQ
  LED led_1 (.in(d_ff_1_q[1]));
  LED led_2 (.in(d_ff_1_q[2]));
  LED led_3 (.in(d_ff_1_q[0]));

  // Notes on the sheet:
  //   contents of rom_1 (hex, n*v repeats v):
  //   1,4,0,6,3
endmodule
