// Digital circuit seta_de_carro.dig as structural Verilog
module seta_de_carro (
  input  RIGHT,
  input  H,
  input  clk,
  input  LEFT
);

  wire [2:0] d_ff_3_q, d_ff_6_q, multiplexer_1_out, multiplexer_2_out, rom_1_d, rom_2_d, rom_3_d;

  ROM #(.AddrBits(4), .Bits(3)) rom_1 (.A({LEFT, d_ff_6_q}), .sel(1'b1), .D(rom_1_d));
  ROM #(.AddrBits(3), .Bits(3)) rom_2 (.A(d_ff_3_q), .sel(1'b1), .D(rom_2_d));
  ROM #(.AddrBits(4), .Bits(3)) rom_3 (.A({RIGHT, d_ff_3_q}), .sel(1'b1), .D(rom_3_d));
  Multiplexer #(.Bits(3)) multiplexer_1 (.sel(H), .in_0(rom_1_d), .in_1(rom_2_d), .out(multiplexer_1_out));
  Multiplexer #(.Bits(3)) multiplexer_2 (.sel(H), .in_0(rom_3_d), .in_1(rom_2_d), .out(multiplexer_2_out));
  D_FF d_ff_1 (.D(multiplexer_2_out[0]), .C(clk), .Q(d_ff_3_q[0]));  // open: nQ
  D_FF d_ff_2 (.D(multiplexer_2_out[1]), .C(clk), .Q(d_ff_3_q[1]));  // open: nQ
  D_FF d_ff_3 (.D(multiplexer_2_out[2]), .C(clk), .Q(d_ff_3_q[2]));  // open: nQ
  D_FF d_ff_4 (.D(multiplexer_1_out[0]), .C(clk), .Q(d_ff_6_q[0]));  // open: nQ
  D_FF d_ff_5 (.D(multiplexer_1_out[1]), .C(clk), .Q(d_ff_6_q[1]));  // open: nQ
  D_FF d_ff_6 (.D(multiplexer_1_out[2]), .C(clk), .Q(d_ff_6_q[2]));  // open: nQ
  LED led_1 (.in(d_ff_6_q[0]));
  LED led_2 (.in(d_ff_6_q[1]));
  LED led_3 (.in(d_ff_6_q[2]));
  LED led_4 (.in(d_ff_3_q[0]));
  LED led_5 (.in(d_ff_3_q[1]));
  LED led_6 (.in(d_ff_3_q[2]));

  // Notes on the sheet:
  //   contents of rom_1 (hex, n*v repeats v):
  //   8*0,4,0,0,0,6,0,7
  //   contents of rom_2 (hex, n*v repeats v):
  //   7
  //   contents of rom_3 (hex, n*v repeats v):
  //   8*0,1,3,0,7
endmodule
